// Logisim project MIPS_Pipelined_Hazards_Logisim.circ as structural Verilog: 17 circuits, main circuit main
module main (
  input  in_1,
  input  in_2,
  output [31:0] out_3
);

  wire BRANCH_EX, BRANCH_ID, BRANCH_ME, BRANCH_SUCCESS, clk, clock_1_out, comparator_1_eq, HALT_EX, HALT_ID,
       HALT_ME, HALT_WB, JAL_EX, JAL_ID, JAL_ME, JAL_WB, JR_EX, JR_ID, JR_ME, JR_WB, JUMP_EX, JUMP_ID,
       JUMP_ME, JUMP_WB, MEM_TO_REG_EX, MEM_TO_REG_ID, MEM_TO_REG_ME, MEM_TO_REG_WB, MEMWRITE_EX,
       MEMWRITE_ID, MEMWRITE_ME, not_1_out, PRINT_TO_SCREEN_EX, PRINT_TO_SCREEN_ID, PRINT_TO_SCREEN_ME,
       PRINT_TO_SCREEN_WB, REGWRITE_EX, REGWRITE_ID, REGWRITE_ME, REGWRITE_WB, STALL, ZERO_BIT_EX,
       ZERO_BIT_ME;
  wire [1:0] ALUSRC_EX, ALUSRC_ID, FORWARD_A, FORWARD_B, REGDST_EX, REGDST_ID;
  wire [3:0] ALUOP_EX, ALUOP_ID, counter_2_q, counter_2_q_2;
  wire [4:0] ADDRESS_RD_EX, ADDRESS_RD_ID, ADDRESS_REGWRITE_EX, ADDRESS_REGWRITE_ME, ADDRESS_REGWRITE_WB,
       ADDRESS_RS_EX, ADDRESS_RS_ID, ADDRESS_RT_EX, ADDRESS_RT_ID, ADDRESS_RT_ME,
       instruction_splitter_1_shamt;
  wire [5:0] FUNCT, OPCODE;
  wire [15:0] IMM_EX, IMM_ID, shifter_3_out;
  wire [23:0] shifter_1_out, shifter_4_out;
  wire [25:0] instruction_splitter_1_address, shifter_2_out;
  wire [31:0] adder_1_out, ALU_RESULT_EX, ALU_RESULT_ME, ALU_RESULT_WB, bit_extender_3_out,
       bit_extender_4_out, bit_extender_5_out, BRANCH_ADDR_EX, BRANCH_ADDR_ME, if_id_1_instid,
       JUMP_ADDRESS_EX, JUMP_ADDRESS_ID, JUMP_ADDRESS_ME, JUMP_ADDRESS_WB, MEM_DATA_ME, MEM_DATA_WB,
       multiplexer_1_out, multiplexer_2_out, multiplexer_3_out, multiplexer_4_out, multiplexer_7_out,
       multiplexer_8_out, multiplexer_12_out, multiplexer_14_out, PC_PLUS_4_IF, PCPLUS4_EX, PCPLUS4_ID,
       PCPLUS4_ME, PCPLUS4_WB, PRINT_VAL, Program_Counter_q, REG_RS_VAL_EX, REG_RS_VAL_EX_NEW, REG_RS_VAL_ID,
       REG_RS_VAL_ME, REG_RS_VAL_WB, REG_RT_VAL_EX, REG_RT_VAL_EX_NEW, REG_RT_VAL_ID, REG_RT_VAL_ME,
       REG_VAL_WRITE, register_1_q, SHAMT_EX, SHAMT_ID;

  Multiplexer #(.width(32), .enable("false")) multiplexer_1 (
    .in0(PC_PLUS_4_IF), .in1(BRANCH_ADDR_ME), .out(multiplexer_1_out), .sel(BRANCH_SUCCESS));
  Clock clock_1 (.out(clock_1_out));
  Multiplexer #(.width(32), .enable("false")) multiplexer_2 (
    .in0(multiplexer_1_out), .in1(JUMP_ADDRESS_WB), .out(multiplexer_2_out), .sel(JUMP_WB));
  Multiplexer #(.width(32), .enable("false")) multiplexer_3 (
    .in0(multiplexer_2_out), .in1(JUMP_ADDRESS_WB), .out(multiplexer_3_out), .sel(JAL_WB));
  Multiplexer #(.width(32), .enable("false")) multiplexer_4 (
    .in0(multiplexer_3_out), .in1(ALU_RESULT_WB), .out(multiplexer_4_out), .sel(JR_WB));
  Counter counter_1 (.clk(clock_1_out), .clr(in_2));  // open: load, D, count, Q, carry
  Register #(.width(32)) Program_Counter (
    .D(multiplexer_4_out), .Q(Program_Counter_q), .clk(clk), .clr(in_2));  // open: en
  Multiplexer #(.enable("false")) multiplexer_5 (.in0(clock_1_out), .in1(1'b0), .out(clk), .sel(HALT_WB));
  Counter counter_2 (
    .D({counter_2_q_2, counter_2_q}), .Q({counter_2_q_2, counter_2_q}), .clk(clock_1_out));  // open: load, count, carry, clr
  Shifter #(.width(24), .shift("lr")) shifter_1 (.in(Program_Counter_q[23:0]), .\dist (5'b00010), .out(shifter_1_out));
  Hex_Digit_Display hex_digit_display_1 (.value(counter_2_q_2));  // open: dp
  Adder #(.width(32)) adder_1 (.a(Program_Counter_q), .b(32'h4), .out(adder_1_out));  // open: cin, cout
  Hex_Digit_Display hex_digit_display_2 (.value(counter_2_q));  // open: dp
  ROM #(.addrWidth(24), .dataWidth(32)) rom_1 (.addr(shifter_1_out), .data(out_3));  // open: sel
  Multiplexer #(.width(32), .enable("false")) multiplexer_6 (
    .in0(Program_Counter_q), .in1(adder_1_out), .out(PC_PLUS_4_IF), .sel(not_1_out));
  not not_1 (not_1_out, STALL);
  Hazard_Unit hazard_unit_1 (
    .CLOCK(clk), .EX_MEM_REGWRITE(REGWRITE_ME), .MEM_WB_REGWRITE(REGWRITE_WB),
    .EX_MEM_REGISTER_RD(ADDRESS_REGWRITE_ME), .ID_EX_REGISTER_RS(ADDRESS_RS_EX), .ID_OPCODE(OPCODE),
    .ID_EX_REGISTER_RT(ADDRESS_RT_EX), .MEM_WB_REGISTER_RD(ADDRESS_REGWRITE_WB), .FORWARD_A(FORWARD_A),
    .STALL(STALL), .FORWARD_B(FORWARD_B), .ID_EX_MEMWRITE(MEMWRITE_EX));
  Hex_Digit_Display hex_digit_display_3 (.value(PRINT_VAL[27:24]));  // open: dp
  Hex_Digit_Display hex_digit_display_4 (.value(PRINT_VAL[31:28]));  // open: dp
  IF_ID if_id_1 (
    .CLEAR(in_2), .InstIF(out_3), .PCPlus4ID(PC_PLUS_4_IF), .InstID(if_id_1_instid), .PCPlus4IF(PCPLUS4_ID),
    .CLOCK(clk), .Stall(STALL));
  Hex_Digit_Display hex_digit_display_5 (.value(PRINT_VAL[23:20]));  // open: dp
  Hex_Digit_Display hex_digit_display_6 (.value(PRINT_VAL[19:16]));  // open: dp
  Instruction_Splitter instruction_splitter_1 (
    .in_1(multiplexer_7_out), .Function(FUNCT), .Shamt(instruction_splitter_1_shamt),
    .Constant_Address(IMM_ID), .Reg_read_rd(ADDRESS_RD_ID), .Address(instruction_splitter_1_address),
    .Reg_read_rt(ADDRESS_RT_ID), .Reg_read_rs(ADDRESS_RS_ID), .Opcode(OPCODE));
  Multiplexer #(.width(32), .enable("false")) multiplexer_7 (
    .in0(if_id_1_instid), .in1({32{1'b1}}), .out(multiplexer_7_out), .sel(in_1));
  Hex_Digit_Display hex_digit_display_7 (.value(PRINT_VAL[15:12]));  // open: dp
  Hex_Digit_Display hex_digit_display_8 (.value(PRINT_VAL[11:8]));  // open: dp
  Control_Unit control_unit_1 (
    .Opcode(OPCODE), .Funct(FUNCT), .JUMP(JUMP_ID), .JAL(JAL_ID), .JR(JR_ID), .REGDST(REGDST_ID),
    .REGWRITE(REGWRITE_ID), .MEMWRITE(MEMWRITE_ID), .HALT(HALT_ID), .MEM_TO_REG(MEM_TO_REG_ID),
    .PRINT_TO_SCREEN(PRINT_TO_SCREEN_ID), .BRANCH(BRANCH_ID), .ALUSRC(ALUSRC_ID), .ALUOP(ALUOP_ID));
  Hex_Digit_Display hex_digit_display_9 (.value(PRINT_VAL[3:0]));  // open: dp
  Hex_Digit_Display hex_digit_display_10 (.value(PRINT_VAL[7:4]));  // open: dp
  assign SHAMT_ID = {{27{1'b0}}, instruction_splitter_1_shamt};  // Bit_Extender bit_extender_1
  Shifter #(.width(26)) shifter_2 (.in(instruction_splitter_1_address), .\dist (5'b00010), .out(shifter_2_out));
  _32reg32 u_32reg32_1 (
    .Read_0(ADDRESS_RS_ID), .Read_1(ADDRESS_RT_ID), .write_addr(ADDRESS_REGWRITE_WB), .RegWrite(REGWRITE_WB),
    .Value_0(REG_RS_VAL_ID), .Value_1(REG_RT_VAL_ID), .RegClear(in_2), .Clock(clk),
    .write_value(REG_VAL_WRITE));
  assign JUMP_ADDRESS_ID = {{6{1'b0}}, shifter_2_out};  // Bit_Extender bit_extender_2
  Multiplexer #(.width(32), .enable("false")) multiplexer_8 (
    .in0({32{1'b0}}), .in1(REG_RS_VAL_WB), .out(multiplexer_8_out), .sel(PRINT_TO_SCREEN_WB));
  Multiplexer #(.width(32), .enable("false")) multiplexer_9 (
    .in0(multiplexer_8_out), .in1(register_1_q), .out(PRINT_VAL), .sel(HALT_WB));
  Register #(.width(32)) register_1 (.D(PRINT_VAL), .Q(register_1_q), .clk(clk));  // open: en, clr
  ID_EX id_ex_1 (
    .PCPLUS4_ID(PCPLUS4_ID), .REG_RS_VAL_ID(REG_RS_VAL_ID), .SHAMT_ID(SHAMT_ID),
    .REG_RT_VAL_ID(REG_RT_VAL_ID), .JUMP_ADDR_ID(JUMP_ADDRESS_ID), .REGDST_ID(REGDST_ID), .IMM_ID(IMM_ID),
    .REG_RD_ID(ADDRESS_RD_ID), .ALUOP_ID(ALUOP_ID), .REG_RT_ID(ADDRESS_RT_ID), .BRANCH_ID(BRANCH_ID),
    .MEMWRITE_ID(MEMWRITE_ID), .REGWRITE_ID(REGWRITE_ID), .JR_ID(JR_ID), .JAL_ID(JAL_ID),
    .ALUSRC_ID(ALUSRC_ID), .MEM_TO_REG_ID(MEM_TO_REG_ID), .PCPLUS4_EX(PCPLUS4_EX),
    .REG_RS_VAL_EX(REG_RS_VAL_EX), .SHAMT_EX(SHAMT_EX), .REG_RT_VAL_EX(REG_RT_VAL_EX),
    .JUMP_ADDR_EX(JUMP_ADDRESS_EX), .REGDST_EX(REGDST_EX), .IMM_EX(IMM_EX), .REG_RD_EX(ADDRESS_RD_EX),
    .ALUOP_EX(ALUOP_EX), .REG_RT_EX(ADDRESS_RT_EX), .BRANCH_EX(BRANCH_EX), .MEMWRITE_EX(MEMWRITE_EX),
    .REGWRITE_EX(REGWRITE_EX), .JR_EX(JR_EX), .JAL_EX(JAL_EX), .ALUSRC_EX(ALUSRC_EX),
    .MEM_TO_REG_EX(MEM_TO_REG_EX), .CLOCK(clk), .CLEAR(in_2), .STALL(1'b0), .HALT_ID(HALT_ID),
    .PRINT_SC_ID(PRINT_TO_SCREEN_ID), .PRINT_SC_EX(PRINT_TO_SCREEN_EX), .HALT_EX(HALT_EX), .J_ID(JUMP_ID),
    .J_EX(JUMP_EX), .REG_RS_ID(ADDRESS_RS_ID), .REG_RS_EX(ADDRESS_RS_EX));
  Shifter #(.width(16)) shifter_3 (.in(IMM_EX), .\dist (4'b0010), .out(shifter_3_out));
  assign bit_extender_3_out = {{16{shifter_3_out[15]}}, shifter_3_out};  // Bit_Extender bit_extender_3
  Multiplexer #(.select(2), .width(32), .enable("false")) multiplexer_10 (
    .in0(REG_RS_VAL_EX), .in1(REG_VAL_WRITE), .in2(ALU_RESULT_ME), .out(REG_RS_VAL_EX_NEW), .sel(FORWARD_A));  // open: in3
  assign bit_extender_4_out = {{16{IMM_EX[15]}}, IMM_EX};  // Bit_Extender bit_extender_4
  assign bit_extender_5_out = {{16{1'b0}}, IMM_EX};  // Bit_Extender bit_extender_5
  Multiplexer #(.select(2), .width(32), .enable("false")) multiplexer_11 (
    .in0(REG_RT_VAL_EX), .in1(REG_VAL_WRITE), .in2(ALU_RESULT_ME), .in3(REG_VAL_WRITE),
    .out(REG_RT_VAL_EX_NEW), .sel(FORWARD_B));
  Adder #(.width(32)) adder_2 (.a(bit_extender_3_out), .b(PCPLUS4_EX), .out(BRANCH_ADDR_EX));  // open: cin, cout
  DSDSSDS dsdssds_1 (
    .A(REG_RS_VAL_EX_NEW), .B(multiplexer_12_out), .ALUOP(ALUOP_EX), .Zero_Bit(ZERO_BIT_EX),
    .Result(ALU_RESULT_EX));
  Multiplexer #(.select(2), .width(32), .enable("false")) multiplexer_12 (
    .in0(REG_RT_VAL_EX_NEW), .in1(bit_extender_4_out), .in2(bit_extender_5_out), .in3(SHAMT_EX),
    .out(multiplexer_12_out), .sel(ALUSRC_EX));
  Multiplexer #(.select(2), .width(5), .enable("false")) multiplexer_13 (
    .in0(ADDRESS_RT_EX), .in1(ADDRESS_RD_EX), .in2({5{1'b1}}), .out(ADDRESS_REGWRITE_EX), .sel(REGDST_EX));  // open: in3
  EX_ME ex_me_1 (
    .BRANCH_ADDR_EX(BRANCH_ADDR_EX), .JUMP_ADDR_EX(JUMP_ADDRESS_EX), .REG_RT_VAL_EX(REG_RT_VAL_EX_NEW),
    .ZERO_BIT_EX(ZERO_BIT_EX), .ALURESULT_EX(ALU_RESULT_EX), .REG_WRITE_ID_EX(ADDRESS_REGWRITE_EX),
    .BRANCH_EX(BRANCH_EX), .MEMWRITE_EX(MEMWRITE_EX), .REGWRITE_EX(REGWRITE_EX), .JR_EX(JR_EX),
    .JAL_EX(JAL_EX), .MEM_TO_REG_EX(MEM_TO_REG_EX), .BRANCH_ADDR_ME(BRANCH_ADDR_ME),
    .JUMP_ADDR_ME(JUMP_ADDRESS_ME), .REG_RT_VAL_ME(REG_RT_VAL_ME), .ZERO_BIT_ME(ZERO_BIT_ME),
    .ALURESULT_ME(ALU_RESULT_ME), .REG_WRITE_ID_ME(ADDRESS_REGWRITE_ME), .BRANCH_ME(BRANCH_ME),
    .MEMWRITE_ME(MEMWRITE_ME), .REGWRITE_ME(REGWRITE_ME), .JR_ME(JR_ME), .JAL_ME(JAL_ME),
    .MEM_TO_REG_ME(MEM_TO_REG_ME), .CLOCK(clk), .CLEAR(in_2), .STALL(1'b0), .PC_PLUS4_EX(PCPLUS4_EX),
    .PC_PLUS4_ME(PCPLUS4_ME), .REG_RS_VAL_ME(REG_RS_VAL_ME), .REG_RS_VAL_EX(REG_RS_VAL_EX_NEW),
    .PRINT_SC_EX(PRINT_TO_SCREEN_EX), .PRINT_SC_ME(PRINT_TO_SCREEN_ME), .HALT_EX(HALT_EX), .HALT_ME(HALT_ME),
    .J_EX(JUMP_EX), .J_ME(JUMP_ME), .REG_RT_ADDR_EX(ADDRESS_RT_EX), .REG_RT_ADDR_ME(ADDRESS_RT_ME));
  and and_1 (BRANCH_SUCCESS, BRANCH_ME, ZERO_BIT_ME);
  Shifter #(.width(24), .shift("lr")) shifter_4 (.in(ALU_RESULT_ME[23:0]), .\dist (5'b00010), .out(shifter_4_out));
  Comparator #(.width(5)) comparator_1 (
    .a(ADDRESS_RT_ME), .b(ADDRESS_REGWRITE_WB), .eq(comparator_1_eq));  // open: gt, lt
  // AND_Gate and_2 has open pins: in0=comparator_1_eq, in1=MEMWRITE_ME, in2=REGWRITE_WB, out=open
  RAM #(.addrWidth(24), .dataWidth(32), .bus("separate")) ram_1 (
    .addr(shifter_4_out), .din(REG_RT_VAL_ME), .data(MEM_DATA_ME), .str(MEMWRITE_ME), .sel(1'b1), .clk(clk),
    .ld(1'b1));  // open: clr
  ME_WB me_wb_1 (
    .JUMP_ADDR_ME(JUMP_ADDRESS_ME), .ALURESULT_ME(ALU_RESULT_ME), .REG_WRITE_ID_ME(ADDRESS_REGWRITE_ME),
    .REGWRITE_ME(REGWRITE_ME), .JR_ME(JR_ME), .JAL_ME(JAL_ME), .MEM_TO_REG_ME(MEM_TO_REG_ME),
    .JUMP_ADDR_WB(JUMP_ADDRESS_WB), .ALURESULT_WB(ALU_RESULT_WB), .REG_WRITE_ID_WB(ADDRESS_REGWRITE_WB),
    .REGWRITE_WB(REGWRITE_WB), .JR_WB(JR_WB), .JAL_WB(JAL_WB), .MEM_TO_REG_WB(MEM_TO_REG_WB), .CLOCK(clk),
    .CLEAR(in_2), .STALL(1'b0), .MEM_DATA_ME(MEM_DATA_ME), .MEM_DATA_WB(MEM_DATA_WB),
    .PC_PLUS4_ME(PCPLUS4_ME), .PC_PLUS4_WB(PCPLUS4_WB), .REG_RS_VAL_ME(REG_RS_VAL_ME),
    .REG_RS_VAL_WB(REG_RS_VAL_WB), .PRINT_SC_ME(PRINT_TO_SCREEN_ME), .PRINT_SC_WB(PRINT_TO_SCREEN_WB),
    .HALT_ME(HALT_ME), .HALT_WB(HALT_WB), .J_ME(JUMP_ME), .J_WB(JUMP_WB));
  Multiplexer #(.width(32), .enable("false")) multiplexer_14 (
    .in0(ALU_RESULT_WB), .in1(MEM_DATA_WB), .out(multiplexer_14_out), .sel(MEM_TO_REG_WB));
  Multiplexer #(.width(32), .enable("false")) multiplexer_15 (
    .in0(multiplexer_14_out), .in1(PCPLUS4_WB), .out(REG_VAL_WRITE), .sel(JAL_WB));

  // Other names for the same wires on the sheet: Clear_PC = in_2

  // Notes on the sheet:
  //   BRANCH
  //   J
  //   JAL
  //   JR
  //   contents of rom_1 (hex, n*v repeats v):
  //   8020 8820 2008000a 208482a 11200003 2308820 22100001 8000003
endmodule

// CONTROL UNIT
module Control_Unit (
  input  [5:0] Opcode,
  input  [5:0] Funct,
  output JUMP,
  output JAL,
  output JR,
  output [1:0] REGDST,
  output REGWRITE,
  output MEMWRITE,
  output HALT,
  output MEM_TO_REG,
  output PRINT_TO_SCREEN,
  output BRANCH,
  output [1:0] ALUSRC,
  output [3:0] ALUOP
);

  wire not_1_out, not_2_out, not_3_out, not_4_out, not_5_out, not_6_out, Opcode_OR_Funct;
  wire [5:0] FunctMUX, OpMUX;

  not not_1 (not_1_out, Opcode[5]);
  not not_2 (not_2_out, Opcode[4]);
  not not_3 (not_3_out, Opcode[3]);
  not not_4 (not_4_out, Opcode[2]);
  not not_5 (not_5_out, Opcode[1]);
  not not_6 (not_6_out, Opcode[0]);
  Control_Decoder control_decoder_1 (
    .S5(Opcode[5]), .S4(Opcode[4]), .S3(Opcode[3]), .S2(Opcode[2]), .S1(Opcode[1]), .S0(Opcode[0]),
    .ALUOP3(OpMUX[5]), .ALUOP2(OpMUX[4]), .ALUOP1(OpMUX[3]), .ALUOP0(OpMUX[2]), .JUMP(JUMP), .JAL(JAL),
    .JR(JR), .ALUSRC1(OpMUX[1]), .ALUSRC0(OpMUX[0]), .REGDST1(REGDST[1]), .REGDST0(REGDST[0]),
    .REGWRITE(REGWRITE), .MEMWRITE(MEMWRITE), .MEM_TO_REG(MEM_TO_REG), .BRANCH(BRANCH), .HALT(HALT),
    .PRINT_TO_SCREEN(PRINT_TO_SCREEN));
  Funct_Decoder funct_decoder_1 (
    .F5(Funct[5]), .F4(Funct[4]), .F3(Funct[3]), .F2(Funct[2]), .F1(Funct[1]), .F0(Funct[0]),
    .ALUOP3(FunctMUX[5]), .ALUOP2(FunctMUX[4]), .ALUOP1(FunctMUX[3]), .ALUOP0(FunctMUX[2]),
    .ALUSRC1(FunctMUX[1]), .ALUSRC0(FunctMUX[0]));
  and and_1 (Opcode_OR_Funct, not_1_out, not_2_out, not_3_out, not_4_out, not_5_out, not_6_out);
  Multiplexer #(.width(6), .enable("false")) multiplexer_1 (
    .in0(OpMUX), .in1(FunctMUX), .out({ALUOP, ALUSRC}), .sel(Opcode_OR_Funct));
endmodule

module Control_Decoder (
  input  S5,
  input  S4,
  input  S3,
  input  S2,
  input  S1,
  input  S0,
  output ALUOP3,
  output ALUOP2,
  output ALUOP1,
  output ALUOP0,
  output JUMP,
  output JAL,
  output JR,
  output ALUSRC1,
  output ALUSRC0,
  output REGDST1,
  output REGDST0,
  output REGWRITE,
  output MEMWRITE,
  output MEM_TO_REG,
  output BRANCH,
  output HALT,
  output PRINT_TO_SCREEN
);

  wire and_6_out, and_7_out, and_8_out, and_9_out, and_10_out, and_11_out, and_12_out, and_13_out,
       and_14_out, and_15_out, and_16_out, and_17_out, and_18_out, and_19_out, and_22_out, and_23_out,
       and_24_out, and_25_out, and_26_out, and_27_out, and_28_out, and_29_out, and_30_out, and_31_out,
       and_32_out, and_33_out, and_34_out, and_35_out, not_1_out, not_2_out, not_3_out, not_4_out, not_5_out,
       not_6_out, not_7_out, not_8_out, not_9_out, not_10_out, not_11_out, not_12_out, not_13_out,
       not_14_out, not_15_out, not_16_out, not_17_out, not_18_out, not_19_out, not_20_out, not_21_out,
       not_22_out, not_23_out, not_24_out, not_25_out, not_26_out, not_27_out, not_28_out, not_29_out,
       not_30_out, not_31_out, not_32_out, not_33_out, not_34_out, not_35_out, not_36_out, not_37_out,
       not_38_out, not_39_out, not_40_out, not_41_out, not_42_out, not_43_out, not_44_out, not_45_out,
       not_46_out, not_47_out, not_48_out, not_49_out, not_50_out, not_51_out, not_52_out, not_53_out,
       not_54_out, not_55_out, not_56_out, not_57_out, not_58_out, not_59_out, not_60_out, not_61_out,
       not_62_out, not_63_out, not_64_out, not_65_out, not_66_out, not_67_out;

  not not_1 (not_1_out, S2);
  not not_2 (not_2_out, S3);
  not not_3 (not_3_out, S1);
  not not_4 (not_4_out, S3);
  not not_5 (not_5_out, S2);
  and and_1 (MEMWRITE, S5, S3, not_1_out);
  and and_2 (BRANCH, not_2_out, S2, not_3_out);
  and and_3 (HALT, not_4_out, S2, S1);
  and and_4 (PRINT_TO_SCREEN, S4, not_5_out);
  not not_6 (not_6_out, S5);
  not not_7 (not_7_out, S4);
  not not_8 (not_8_out, S3);
  not not_9 (not_9_out, S2);
  not not_10 (not_10_out, S1);
  not not_11 (not_11_out, S3);
  not not_12 (not_12_out, S1);
  not not_13 (not_13_out, S5);
  not not_14 (not_14_out, S4);
  not not_15 (not_15_out, S1);
  not not_16 (not_16_out, S4);
  not not_17 (not_17_out, S2);
  not not_18 (not_18_out, S5);
  not not_19 (not_19_out, S2);
  not not_20 (not_20_out, S1);
  not not_21 (not_21_out, S4);
  not not_22 (not_22_out, S3);
  not not_23 (not_23_out, S1);
  not not_24 (not_24_out, S1);
  not not_25 (not_25_out, S5);
  not not_26 (not_26_out, S2);
  not not_27 (not_27_out, S4);
  not not_28 (not_28_out, S2);
  not not_29 (not_29_out, S1);
  not not_30 (not_30_out, S0);
  not not_31 (not_31_out, S5);
  not not_32 (not_32_out, S4);
  not not_33 (not_33_out, S3);
  not not_34 (not_34_out, S2);
  not not_35 (not_35_out, S5);
  not not_36 (not_36_out, S4);
  not not_37 (not_37_out, S3);
  not not_38 (not_38_out, S2);
  not not_39 (not_39_out, S5);
  not not_40 (not_40_out, S3);
  not not_41 (not_41_out, S2);
  not not_42 (not_42_out, S3);
  not not_43 (not_43_out, S1);
  and and_5 (ALUSRC1, S3, S2);
  not not_44 (not_44_out, S2);
  not not_45 (not_45_out, S5);
  not not_46 (not_46_out, S3);
  not not_47 (not_47_out, S5);
  not not_48 (not_48_out, S3);
  not not_49 (not_49_out, S5);
  not not_50 (not_50_out, S3);
  not not_51 (not_51_out, S5);
  not not_52 (not_52_out, S3);
  not not_53 (not_53_out, S4);
  not not_54 (not_54_out, S3);
  not not_55 (not_55_out, S2);
  not not_56 (not_56_out, S1);
  not not_57 (not_57_out, S0);
  not not_58 (not_58_out, S1);
  not not_59 (not_59_out, S0);
  not not_60 (not_60_out, S5);
  not not_61 (not_61_out, S4);
  not not_62 (not_62_out, S2);
  not not_63 (not_63_out, S1);
  not not_64 (not_64_out, S0);
  not not_65 (not_65_out, S4);
  not not_66 (not_66_out, S3);
  not not_67 (not_67_out, S5);
  and and_6 (and_6_out, not_6_out, not_7_out, not_8_out, not_9_out, not_10_out);
  and and_7 (and_7_out, not_11_out, not_12_out, S0);
  and and_8 (and_8_out, not_13_out, S3, S1);
  and and_9 (and_9_out, not_14_out, not_15_out);
  or or_1 (ALUOP2, and_9_out, and_10_out, and_11_out);
  and and_10 (and_10_out, not_16_out, S2, S0);
  and and_11 (and_11_out, S5, not_17_out);
  and and_12 (and_12_out, not_18_out, S3, not_19_out, S1);
  and and_13 (and_13_out, S3, S2, not_20_out);
  and and_14 (and_14_out, not_21_out, not_22_out, not_23_out);
  and and_15 (and_15_out, S2, not_24_out, S0);
  and and_16 (and_16_out, not_25_out, S3, not_26_out, S1, S0);
  and and_17 (and_17_out, S5, not_27_out, not_28_out, not_29_out, not_30_out);
  and and_18 (and_18_out, not_31_out, not_32_out, not_33_out, not_34_out, S0);
  and and_19 (and_19_out, not_35_out, not_36_out, not_37_out, not_38_out, S1);
  and and_20 (JAL, not_39_out, not_40_out, not_41_out, S0);
  and and_21 (JR, not_42_out, not_43_out, S0);
  and and_22 (and_22_out, S3, not_44_out);
  or or_2 (ALUSRC0, and_22_out, S5);
  and and_23 (and_23_out, not_45_out, not_46_out, S0);
  and and_24 (and_24_out, not_47_out, not_48_out, S1);
  and and_25 (and_25_out, not_49_out, not_50_out, S2);
  and and_26 (and_26_out, not_51_out, S4, not_52_out);
  and and_27 (and_27_out, not_53_out, not_54_out, not_55_out, not_56_out, not_57_out);
  and and_28 (and_28_out, S5, not_58_out);
  and and_29 (and_29_out, S5, not_59_out);
  and and_30 (and_30_out, S5, S2);
  and and_31 (and_31_out, S5, S3);
  and and_32 (and_32_out, S5, S4);
  and and_33 (and_33_out, not_60_out, not_61_out, not_62_out, not_63_out, not_64_out);
  and and_34 (and_34_out, not_65_out, not_66_out, S1, S0);
  and and_35 (and_35_out, not_67_out, S3);
  or or_3 (ALUOP3, and_6_out, and_7_out, and_8_out);
  or or_4 (ALUOP1, and_12_out, and_13_out);
  or or_5 (ALUOP0, and_14_out, and_15_out, and_16_out, and_17_out);
  or or_6 (JUMP, and_18_out, and_19_out);
  or or_7 (REGDST1, and_23_out, and_24_out, and_25_out, and_26_out);
  or or_8 (REGDST0, and_27_out, and_28_out, and_29_out, and_30_out, and_31_out, and_32_out);
  or or_9 (REGWRITE, and_33_out, and_34_out, and_35_out);

  assign MEM_TO_REG = S5;
endmodule

module Funct_Decoder (
  input  F5,
  input  F4,
  input  F3,
  input  F2,
  input  F1,
  input  F0,
  output ALUOP3,
  output ALUOP2,
  output ALUOP1,
  output ALUOP0,
  output ALUSRC1,
  output ALUSRC0
);

  wire and_1_out, and_2_out, and_3_out, and_4_out, and_5_out, and_6_out, and_7_out, and_8_out, and_9_out,
       and_10_out, and_11_out, not_1_out, not_2_out, not_3_out, not_4_out, not_5_out, not_6_out, not_7_out,
       not_8_out, not_9_out, not_10_out, not_11_out;

  not not_1 (not_1_out, F0);
  not not_2 (not_2_out, F1);
  not not_3 (not_3_out, F1);
  not not_4 (not_4_out, F3);
  not not_5 (not_5_out, F2);
  not not_6 (not_6_out, F5);
  not not_7 (not_7_out, F1);
  not not_8 (not_8_out, F5);
  not not_9 (not_9_out, F1);
  not not_10 (not_10_out, F3);
  not not_11 (not_11_out, F2);
  not not_12 (ALUSRC1, F5);
  not not_13 (ALUSRC0, F5);
  and and_1 (and_1_out, F2, F1);
  and and_2 (and_2_out, F3, not_1_out);
  and and_3 (and_3_out, F3, F1);
  and and_4 (and_4_out, F2, not_2_out);
  and and_5 (and_5_out, F3, not_3_out);
  and and_6 (and_6_out, F5, not_4_out, not_5_out);
  and and_7 (and_7_out, not_6_out, F1);
  and and_8 (and_8_out, F2, not_7_out);
  and and_9 (and_9_out, F5, F3);
  and and_10 (and_10_out, not_8_out, not_9_out);
  and and_11 (and_11_out, F5, not_10_out, not_11_out, F1);
  or or_1 (ALUOP3, and_1_out, and_2_out, and_3_out);
  or or_2 (ALUOP2, and_4_out, and_5_out, and_6_out);
  or or_3 (ALUOP1, and_7_out, and_8_out, and_9_out);
  or or_4 (ALUOP0, and_10_out, F0, and_11_out);
endmodule

// REGISTER FILE
module _32reg32 (
  input  [4:0] Read_0,
  input  [4:0] Read_1,
  input  [4:0] write_addr,
  input  [31:0] write_value,
  input  Clock,
  input  RegClear,
  input  RegWrite,
  output [31:0] Value_0,
  output [31:0] Value_1
);

  wire and_1_out, and_2_out, and_3_out, and_4_out, and_5_out, and_6_out, and_7_out, and_8_out, and_9_out,
       and_10_out, and_11_out, and_12_out, and_13_out, and_14_out, and_15_out, and_16_out, and_17_out,
       and_18_out, and_19_out, and_20_out, and_21_out, and_22_out, and_23_out, and_24_out, and_25_out,
       and_26_out, and_27_out, and_28_out, and_29_out, and_30_out, and_31_out, decoder_1_out1,
       decoder_1_out2, decoder_1_out3, decoder_1_out4, decoder_1_out5, decoder_1_out6, decoder_1_out7,
       decoder_1_out8, decoder_1_out9, decoder_1_out10, decoder_1_out11, decoder_1_out12, decoder_1_out13,
       decoder_1_out14, decoder_1_out15, decoder_1_out16, decoder_1_out17, decoder_1_out18, decoder_1_out19,
       decoder_1_out20, decoder_1_out21, decoder_1_out22, decoder_1_out23, decoder_1_out24, decoder_1_out25,
       decoder_1_out26, decoder_1_out27, decoder_1_out28, decoder_1_out29, decoder_1_out30, decoder_1_out31;
  wire [31:0] a0_q, a1_q, a2_q, a3_q, at_q, fp_q, gp_q, k0_q, k1_q, ra_q, s0_q, s1_q, s2_q, s3_q, s4_q, s5_q,
       s6_q, s7_q, sp_q, t0_q, t1_q, t2_q, t3_q, t4_q, t5_q, t6_q, t7_q, t8_q, t9_q, v0_q, v1_q;

  Decoder #(.select(5)) decoder_1 (
    .out1(decoder_1_out1), .out2(decoder_1_out2), .out3(decoder_1_out3), .out4(decoder_1_out4),
    .out5(decoder_1_out5), .out6(decoder_1_out6), .out7(decoder_1_out7), .out8(decoder_1_out8),
    .out9(decoder_1_out9), .out10(decoder_1_out10), .out11(decoder_1_out11), .out12(decoder_1_out12),
    .out13(decoder_1_out13), .out14(decoder_1_out14), .out15(decoder_1_out15), .out16(decoder_1_out16),
    .out17(decoder_1_out17), .out18(decoder_1_out18), .out19(decoder_1_out19), .out20(decoder_1_out20),
    .out21(decoder_1_out21), .out22(decoder_1_out22), .out23(decoder_1_out23), .out24(decoder_1_out24),
    .out25(decoder_1_out25), .out26(decoder_1_out26), .out27(decoder_1_out27), .out28(decoder_1_out28),
    .out29(decoder_1_out29), .out30(decoder_1_out30), .out31(decoder_1_out31), .sel(write_addr));  // open: out0, en
  and and_1 (and_1_out, decoder_1_out1, RegWrite);
  and and_2 (and_2_out, RegWrite, decoder_1_out2);
  and and_3 (and_3_out, RegWrite, decoder_1_out3);
  and and_4 (and_4_out, RegWrite, decoder_1_out4);
  and and_5 (and_5_out, RegWrite, decoder_1_out5);
  and and_6 (and_6_out, RegWrite, decoder_1_out6);
  and and_7 (and_7_out, RegWrite, decoder_1_out7);
  and and_8 (and_8_out, RegWrite, decoder_1_out8);
  and and_9 (and_9_out, RegWrite, decoder_1_out9);
  and and_10 (and_10_out, RegWrite, decoder_1_out10);
  and and_11 (and_11_out, RegWrite, decoder_1_out11);
  and and_12 (and_12_out, RegWrite, decoder_1_out12);
  and and_13 (and_13_out, RegWrite, decoder_1_out13);
  and and_14 (and_14_out, RegWrite, decoder_1_out14);
  and and_15 (and_15_out, RegWrite, decoder_1_out15);
  and and_16 (and_16_out, decoder_1_out16, RegWrite);
  and and_17 (and_17_out, decoder_1_out17, RegWrite);
  and and_18 (and_18_out, decoder_1_out18, RegWrite);
  and and_19 (and_19_out, decoder_1_out19, RegWrite);
  and and_20 (and_20_out, decoder_1_out20, RegWrite);
  and and_21 (and_21_out, decoder_1_out21, RegWrite);
  and and_22 (and_22_out, decoder_1_out22, RegWrite);
  and and_23 (and_23_out, decoder_1_out23, RegWrite);
  and and_24 (and_24_out, decoder_1_out24, RegWrite);
  and and_25 (and_25_out, decoder_1_out25, RegWrite);
  and and_26 (and_26_out, decoder_1_out26, RegWrite);
  and and_27 (and_27_out, decoder_1_out27, RegWrite);
  and and_28 (and_28_out, decoder_1_out28, RegWrite);
  and and_29 (and_29_out, decoder_1_out29, RegWrite);
  and and_30 (and_30_out, decoder_1_out30, RegWrite);
  and and_31 (and_31_out, decoder_1_out31, RegWrite);
  Register #(.width(32)) at (.D(write_value), .en(and_1_out), .Q(at_q), .clk(Clock), .clr(RegClear));
  Register #(.width(32)) v0 (.D(write_value), .en(and_2_out), .Q(v0_q), .clk(Clock), .clr(RegClear));
  Register #(.width(32)) v1 (.D(write_value), .en(and_3_out), .Q(v1_q), .clk(Clock), .clr(RegClear));
  Register #(.width(32)) a0 (.D(write_value), .en(and_4_out), .Q(a0_q), .clk(Clock), .clr(RegClear));
  Register #(.width(32)) a1 (.D(write_value), .en(and_5_out), .Q(a1_q), .clk(Clock), .clr(RegClear));
  Register #(.width(32)) a2 (.D(write_value), .en(and_6_out), .Q(a2_q), .clk(Clock), .clr(RegClear));
  Register #(.width(32)) a3 (.D(write_value), .en(and_7_out), .Q(a3_q), .clk(Clock), .clr(RegClear));
  Register #(.width(32)) t0 (.D(write_value), .en(and_8_out), .Q(t0_q), .clk(Clock), .clr(RegClear));
  Register #(.width(32)) t1 (.D(write_value), .en(and_9_out), .Q(t1_q), .clk(Clock), .clr(RegClear));
  Register #(.width(32)) t2 (.D(write_value), .en(and_10_out), .Q(t2_q), .clk(Clock), .clr(RegClear));
  Register #(.width(32)) t3 (.D(write_value), .en(and_11_out), .Q(t3_q), .clk(Clock), .clr(RegClear));
  Register #(.width(32)) t4 (.D(write_value), .en(and_12_out), .Q(t4_q), .clk(Clock), .clr(RegClear));
  Register #(.width(32)) t5 (.D(write_value), .en(and_13_out), .Q(t5_q), .clk(Clock), .clr(RegClear));
  Register #(.width(32)) t6 (.D(write_value), .en(and_14_out), .Q(t6_q), .clk(Clock), .clr(RegClear));
  Register #(.width(32)) t7 (.D(write_value), .en(and_15_out), .Q(t7_q), .clk(Clock), .clr(RegClear));
  Register #(.width(32)) s0 (.D(write_value), .en(and_16_out), .Q(s0_q), .clk(Clock), .clr(RegClear));
  Register #(.width(32)) s1 (.D(write_value), .en(and_17_out), .Q(s1_q), .clk(Clock), .clr(RegClear));
  Register #(.width(32)) s2 (.D(write_value), .en(and_18_out), .Q(s2_q), .clk(Clock), .clr(RegClear));
  Register #(.width(32)) s3 (.D(write_value), .en(and_19_out), .Q(s3_q), .clk(Clock), .clr(RegClear));
  Register #(.width(32)) s4 (.D(write_value), .en(and_20_out), .Q(s4_q), .clk(Clock), .clr(RegClear));
  Register #(.width(32)) s5 (.D(write_value), .en(and_21_out), .Q(s5_q), .clk(Clock), .clr(RegClear));
  Register #(.width(32)) s6 (.D(write_value), .en(and_22_out), .Q(s6_q), .clk(Clock), .clr(RegClear));
  Register #(.width(32)) s7 (.D(write_value), .en(and_23_out), .Q(s7_q), .clk(Clock), .clr(RegClear));
  Register #(.width(32)) t8 (.D(write_value), .en(and_24_out), .Q(t8_q), .clk(Clock), .clr(RegClear));
  Register #(.width(32)) t9 (.D(write_value), .en(and_25_out), .Q(t9_q), .clk(Clock), .clr(RegClear));
  Register #(.width(32)) k0 (.D(write_value), .en(and_26_out), .Q(k0_q), .clk(Clock), .clr(RegClear));
  Register #(.width(32)) k1 (.D(write_value), .en(and_27_out), .Q(k1_q), .clk(Clock), .clr(RegClear));
  Register #(.width(32)) gp (.D(write_value), .en(and_28_out), .Q(gp_q), .clk(Clock), .clr(RegClear));
  Register #(.width(32)) sp (.D(write_value), .en(and_29_out), .Q(sp_q), .clk(Clock), .clr(RegClear));
  Register #(.width(32)) fp (.D(write_value), .en(and_30_out), .Q(fp_q), .clk(Clock), .clr(RegClear));
  Register #(.width(32)) ra (.D(write_value), .en(and_31_out), .Q(ra_q), .clk(Clock), .clr(RegClear));
  Multiplexer #(.select(5), .width(32)) multiplexer_1 (
    .in0({32{1'b0}}), .in1(at_q), .in2(v0_q), .in3(v1_q), .in4(a0_q), .in5(a1_q), .in6(a2_q), .in7(a3_q),
    .in8(t0_q), .in9(t1_q), .in10(t2_q), .in11(t3_q), .in12(t4_q), .in13(t5_q), .in14(t6_q), .in15(t7_q),
    .in16(s0_q), .in17(s1_q), .in18(s2_q), .in19(s3_q), .in20(s4_q), .in21(s5_q), .in22(s6_q), .in23(s7_q),
    .in24(t8_q), .in25(t9_q), .in26(k0_q), .in27(k1_q), .in28(gp_q), .in29(sp_q), .in30(fp_q), .in31(ra_q),
    .out(Value_0), .sel(Read_0));  // open: en
  Multiplexer #(.select(5), .width(32)) multiplexer_2 (
    .in0({32{1'b0}}), .in1(at_q), .in2(v0_q), .in3(v1_q), .in4(a0_q), .in5(a1_q), .in6(a2_q), .in7(a3_q),
    .in8(t0_q), .in9(t1_q), .in10(t2_q), .in11(t3_q), .in12(t4_q), .in13(t5_q), .in14(t6_q), .in15(t7_q),
    .in16(s0_q), .in17(s1_q), .in18(s2_q), .in19(s3_q), .in20(s4_q), .in21(s5_q), .in22(s6_q), .in23(s7_q),
    .in24(t8_q), .in25(t9_q), .in26(k0_q), .in27(k1_q), .in28(gp_q), .in29(sp_q), .in30(fp_q), .in31(ra_q),
    .out(Value_1), .sel(Read_1));  // open: en
endmodule

module Instruction_Splitter (
  input  [31:0] in_1,
  output [5:0] Function,
  output [4:0] Shamt,
  output [15:0] Constant_Address,
  output [4:0] Reg_read_rd,
  output [25:0] Address,
  output [4:0] Reg_read_rt,
  output [4:0] Reg_read_rs,
  output [5:0] Opcode
);


  assign Address = in_1[25:0];
  assign Constant_Address = in_1[15:0];
  assign Function = in_1[5:0];
  assign Opcode = in_1[31:26];
  assign Reg_read_rd = in_1[15:11];
  assign Reg_read_rs = in_1[25:21];
  assign Reg_read_rt = in_1[20:16];
  assign Shamt = in_1[10:6];
endmodule

// SDSDS
module DSDSSDS (
  input  [31:0] A,
  input  [31:0] B,
  input  [3:0] ALUOP,
  output Zero_Bit,
  output [31:0] Result
);

  wire comparator_1_lt, comparator_2_lt;
  wire [4:0] bit_extender_1_out;
  wire [31:0] adder_1_out, and_1_out, bit_extender_2_out, bit_extender_3_out, nor_1_out, or_1_out,
       shifter_1_out, shifter_2_out, shifter_3_out, shifter_4_out, subtractor_1_out, xor_1_out;

  Bit_Extender #(.in_width(32), .out_width(5)) bit_extender_1 (.in(B), .out(bit_extender_1_out));
  Shifter #(.width(32)) shifter_1 (.in(B), .\dist (5'b10000), .out(shifter_1_out));
  Shifter #(.width(32)) shifter_2 (.in(A), .\dist (bit_extender_1_out), .out(shifter_2_out));
  Shifter #(.width(32), .shift("lr")) shifter_3 (.in(A), .\dist (bit_extender_1_out), .out(shifter_3_out));
  Shifter #(.width(32), .shift("ar")) shifter_4 (.in(A), .\dist (bit_extender_1_out), .out(shifter_4_out));
  Adder #(.width(32)) adder_1 (.a(A), .b(B), .out(adder_1_out));  // open: cin, cout
  Subtractor #(.width(32)) subtractor_1 (.a(A), .b(B), .out(subtractor_1_out));  // open: bin, bout
  assign and_1_out = A & B;  // AND_Gate and_1, 32 bits wide
  assign or_1_out = A | B;  // OR_Gate or_1, 32 bits wide
  assign xor_1_out = A ^ B;  // XOR_Gate xor_1, 32 bits wide
  assign nor_1_out = ~(A | B);  // NOR_Gate nor_1, 32 bits wide
  Comparator #(.width(32)) comparator_1 (.a(A), .b(B), .lt(comparator_1_lt));  // open: gt, eq
  Comparator #(.width(32), .mode("unsigned")) comparator_2 (.a(A), .b(B), .lt(comparator_2_lt));  // open: gt, eq
  assign bit_extender_2_out = {{31{1'b0}}, comparator_1_lt};  // Bit_Extender bit_extender_2
  assign bit_extender_3_out = {{31{1'b0}}, comparator_2_lt};  // Bit_Extender bit_extender_3
  Multiplexer #(.select(4), .width(32), .enable("false")) multiplexer_1 (
    .in0({32{1'b0}}), .in1(shifter_2_out), .in2(shifter_3_out), .in3(shifter_4_out), .in4(adder_1_out),
    .in5(subtractor_1_out), .in6(and_1_out), .in7(or_1_out), .in8(xor_1_out), .in9(nor_1_out),
    .in10(bit_extender_2_out), .in11(bit_extender_3_out), .in12({shifter_1_out[31:16], A[15:0]}), .in13(A),
    .out(Result), .sel(ALUOP));  // open: in14, in15
  Comparator #(.width(32)) comparator_3 (.a({32{1'b0}}), .b(Result), .eq(Zero_Bit));  // open: gt, lt
endmodule

module IF_ID (
  input  CLEAR,
  input  CLOCK,
  input  [31:0] InstIF,
  input  [31:0] PCPlus4ID,
  input  Stall,
  output [31:0] InstID,
  output [31:0] PCPlus4IF
);

  wire not_1_out;
  wire [31:0] multiplexer_1_out;

  Multiplexer #(.width(32), .enable("false")) multiplexer_1 (
    .in0(InstIF), .in1({32{1'b1}}), .out(multiplexer_1_out), .sel(Stall));
  not not_1 (not_1_out, Stall);
  Register #(.width(32)) register_1 (.D(multiplexer_1_out), .Q(InstID), .clk(CLOCK), .clr(CLEAR));  // open: en
  Register #(.width(32)) register_2 (.D(PCPlus4ID), .en(not_1_out), .Q(PCPlus4IF), .clk(CLOCK), .clr(CLEAR));
endmodule

module ID_EX (
  input  CLOCK,
  input  CLEAR,
  input  [31:0] PCPLUS4_ID,
  input  PRINT_SC_ID,
  input  HALT_ID,
  input  [31:0] REG_RS_VAL_ID,
  input  [31:0] SHAMT_ID,
  input  [31:0] REG_RT_VAL_ID,
  input  [31:0] JUMP_ADDR_ID,
  input  [1:0] REGDST_ID,
  input  [15:0] IMM_ID,
  input  [4:0] REG_RS_ID,
  input  [4:0] REG_RD_ID,
  input  [3:0] ALUOP_ID,
  input  [4:0] REG_RT_ID,
  input  BRANCH_ID,
  input  MEMWRITE_ID,
  input  REGWRITE_ID,
  input  JR_ID,
  input  JAL_ID,
  input  J_ID,
  input  [1:0] ALUSRC_ID,
  input  MEM_TO_REG_ID,
  input  STALL,
  output [31:0] PCPLUS4_EX,
  output PRINT_SC_EX,
  output HALT_EX,
  output [31:0] REG_RS_VAL_EX,
  output [31:0] SHAMT_EX,
  output [31:0] REG_RT_VAL_EX,
  output [31:0] JUMP_ADDR_EX,
  output [1:0] REGDST_EX,
  output [15:0] IMM_EX,
  output [4:0] REG_RS_EX,
  output [4:0] REG_RD_EX,
  output [3:0] ALUOP_EX,
  output [4:0] REG_RT_EX,
  output BRANCH_EX,
  output MEMWRITE_EX,
  output REGWRITE_EX,
  output JR_EX,
  output JAL_EX,
  output J_EX,
  output [1:0] ALUSRC_EX,
  output MEM_TO_REG_EX
);

  wire not_1_out;

  Register #(.width(1)) register_1 (.D(PRINT_SC_ID), .en(not_1_out), .Q(PRINT_SC_EX), .clk(CLOCK), .clr(CLEAR));
  Register #(.width(1)) register_2 (.D(HALT_ID), .en(not_1_out), .Q(HALT_EX), .clk(CLOCK), .clr(CLEAR));
  Register #(.width(32)) register_3 (.D(REG_RS_VAL_ID), .en(not_1_out), .Q(REG_RS_VAL_EX), .clk(CLOCK), .clr(CLEAR));
  Register #(.width(32)) register_4 (.D(REG_RT_VAL_ID), .en(not_1_out), .Q(REG_RT_VAL_EX), .clk(CLOCK), .clr(CLEAR));
  Register #(.width(16)) register_5 (.D(IMM_ID), .en(not_1_out), .Q(IMM_EX), .clk(CLOCK), .clr(CLEAR));
  Register #(.width(4)) register_6 (.D(ALUOP_ID), .en(not_1_out), .Q(ALUOP_EX), .clk(CLOCK), .clr(CLEAR));
  Register #(.width(1)) register_7 (.D(BRANCH_ID), .en(not_1_out), .Q(BRANCH_EX), .clk(CLOCK), .clr(CLEAR));
  Register #(.width(1)) register_8 (.D(REGWRITE_ID), .en(not_1_out), .Q(REGWRITE_EX), .clk(CLOCK), .clr(CLEAR));
  Register #(.width(1)) register_9 (.D(JAL_ID), .en(not_1_out), .Q(JAL_EX), .clk(CLOCK), .clr(CLEAR));
  Register #(.width(1)) register_10 (.D(MEM_TO_REG_ID), .en(not_1_out), .Q(MEM_TO_REG_EX), .clk(CLOCK), .clr(CLEAR));
  not not_1 (not_1_out, STALL);
  Register #(.width(32)) register_11 (.D(PCPLUS4_ID), .en(not_1_out), .Q(PCPLUS4_EX), .clk(CLOCK), .clr(CLEAR));
  Register #(.width(32)) register_12 (.D(SHAMT_ID), .en(not_1_out), .Q(SHAMT_EX), .clk(CLOCK), .clr(CLEAR));
  Register #(.width(32)) register_13 (.D(JUMP_ADDR_ID), .en(not_1_out), .Q(JUMP_ADDR_EX), .clk(CLOCK), .clr(CLEAR));
  Register #(.width(2)) register_14 (.D(REGDST_ID), .en(not_1_out), .Q(REGDST_EX), .clk(CLOCK), .clr(CLEAR));
  Register #(.width(5)) register_15 (.D(REG_RS_ID), .en(not_1_out), .Q(REG_RS_EX), .clk(CLOCK), .clr(CLEAR));
  Register #(.width(5)) register_16 (.D(REG_RD_ID), .en(not_1_out), .Q(REG_RD_EX), .clk(CLOCK), .clr(CLEAR));
  Register #(.width(5)) register_17 (.D(REG_RT_ID), .en(not_1_out), .Q(REG_RT_EX), .clk(CLOCK), .clr(CLEAR));
  Register #(.width(1)) register_18 (.D(MEMWRITE_ID), .en(not_1_out), .Q(MEMWRITE_EX), .clk(CLOCK), .clr(CLEAR));
  Register #(.width(1)) register_19 (.D(JR_ID), .en(not_1_out), .Q(JR_EX), .clk(CLOCK), .clr(CLEAR));
  Register #(.width(1)) register_20 (.D(J_ID), .en(not_1_out), .Q(J_EX), .clk(CLOCK), .clr(CLEAR));
  Register #(.width(2)) register_21 (.D(ALUSRC_ID), .en(not_1_out), .Q(ALUSRC_EX), .clk(CLOCK), .clr(CLEAR));
endmodule

module EX_ME (
  input  CLOCK,
  input  CLEAR,
  input  [31:0] BRANCH_ADDR_EX,
  input  [31:0] REG_RS_VAL_EX,
  input  [31:0] PC_PLUS4_EX,
  input  [4:0] REG_RT_ADDR_EX,
  input  [31:0] JUMP_ADDR_EX,
  input  [31:0] REG_RT_VAL_EX,
  input  HALT_EX,
  input  ZERO_BIT_EX,
  input  PRINT_SC_EX,
  input  [31:0] ALURESULT_EX,
  input  [4:0] REG_WRITE_ID_EX,
  input  BRANCH_EX,
  input  MEMWRITE_EX,
  input  REGWRITE_EX,
  input  JR_EX,
  input  JAL_EX,
  input  J_EX,
  input  MEM_TO_REG_EX,
  input  STALL,
  output [31:0] BRANCH_ADDR_ME,
  output [31:0] REG_RS_VAL_ME,
  output [31:0] PC_PLUS4_ME,
  output [4:0] REG_RT_ADDR_ME,
  output [31:0] JUMP_ADDR_ME,
  output [31:0] REG_RT_VAL_ME,
  output HALT_ME,
  output ZERO_BIT_ME,
  output PRINT_SC_ME,
  output [31:0] ALURESULT_ME,
  output [4:0] REG_WRITE_ID_ME,
  output BRANCH_ME,
  output MEMWRITE_ME,
  output REGWRITE_ME,
  output JR_ME,
  output JAL_ME,
  output J_ME,
  output MEM_TO_REG_ME
);

  wire not_1_out;

  Register #(.width(32)) register_1 (.D(REG_RS_VAL_EX), .en(not_1_out), .Q(REG_RS_VAL_ME), .clk(CLOCK), .clr(CLEAR));
  Register #(.width(32)) register_2 (.D(PC_PLUS4_EX), .en(not_1_out), .Q(PC_PLUS4_ME), .clk(CLOCK), .clr(CLEAR));
  Register #(.width(32)) register_3 (.D(REG_RT_VAL_EX), .en(not_1_out), .Q(REG_RT_VAL_ME), .clk(CLOCK), .clr(CLEAR));
  Register #(.width(1)) register_4 (.D(ZERO_BIT_EX), .en(not_1_out), .Q(ZERO_BIT_ME), .clk(CLOCK), .clr(CLEAR));
  Register #(.width(32)) register_5 (.D(ALURESULT_EX), .en(not_1_out), .Q(ALURESULT_ME), .clk(CLOCK), .clr(CLEAR));
  Register #(.width(1)) register_6 (.D(BRANCH_EX), .en(not_1_out), .Q(BRANCH_ME), .clk(CLOCK), .clr(CLEAR));
  Register #(.width(1)) register_7 (.D(REGWRITE_EX), .en(not_1_out), .Q(REGWRITE_ME), .clk(CLOCK), .clr(CLEAR));
  Register #(.width(1)) register_8 (.D(JAL_EX), .en(not_1_out), .Q(JAL_ME), .clk(CLOCK), .clr(CLEAR));
  Register #(.width(1)) register_9 (.D(MEM_TO_REG_EX), .en(not_1_out), .Q(MEM_TO_REG_ME), .clk(CLOCK), .clr(CLEAR));
  not not_1 (not_1_out, STALL);
  Register #(.width(32)) register_10 (.D(BRANCH_ADDR_EX), .en(not_1_out), .Q(BRANCH_ADDR_ME), .clk(CLOCK), .clr(CLEAR));
  Register #(.width(5)) register_11 (.D(REG_RT_ADDR_EX), .en(not_1_out), .Q(REG_RT_ADDR_ME), .clk(CLOCK), .clr(CLEAR));
  Register #(.width(32)) register_12 (.D(JUMP_ADDR_EX), .en(not_1_out), .Q(JUMP_ADDR_ME), .clk(CLOCK), .clr(CLEAR));
  Register #(.width(1)) register_13 (.D(HALT_EX), .en(not_1_out), .Q(HALT_ME), .clk(CLOCK), .clr(CLEAR));
  Register #(.width(1)) register_14 (.D(PRINT_SC_EX), .en(not_1_out), .Q(PRINT_SC_ME), .clk(CLOCK), .clr(CLEAR));
  Register #(.width(5)) register_15 (
    .D(REG_WRITE_ID_EX), .en(not_1_out), .Q(REG_WRITE_ID_ME), .clk(CLOCK), .clr(CLEAR));
  Register #(.width(1)) register_16 (.D(MEMWRITE_EX), .en(not_1_out), .Q(MEMWRITE_ME), .clk(CLOCK), .clr(CLEAR));
  Register #(.width(1)) register_17 (.D(JR_EX), .en(not_1_out), .Q(JR_ME), .clk(CLOCK), .clr(CLEAR));
  Register #(.width(1)) register_18 (.D(J_EX), .en(not_1_out), .Q(J_ME), .clk(CLOCK), .clr(CLEAR));
endmodule

module ME_WB (
  input  CLOCK,
  input  CLEAR,
  input  [31:0] REG_RS_VAL_ME,
  input  [31:0] PC_PLUS4_ME,
  input  [31:0] JUMP_ADDR_ME,
  input  PRINT_SC_ME,
  input  HALT_ME,
  input  [31:0] ALURESULT_ME,
  input  [4:0] REG_WRITE_ID_ME,
  input  J_ME,
  input  REGWRITE_ME,
  input  JR_ME,
  input  JAL_ME,
  input  [31:0] MEM_DATA_ME,
  input  MEM_TO_REG_ME,
  input  STALL,
  output [31:0] REG_RS_VAL_WB,
  output [31:0] PC_PLUS4_WB,
  output [31:0] JUMP_ADDR_WB,
  output PRINT_SC_WB,
  output HALT_WB,
  output [31:0] ALURESULT_WB,
  output [4:0] REG_WRITE_ID_WB,
  output J_WB,
  output REGWRITE_WB,
  output JR_WB,
  output JAL_WB,
  output [31:0] MEM_DATA_WB,
  output MEM_TO_REG_WB
);

  wire not_1_out;

  Register #(.width(32)) register_1 (.D(REG_RS_VAL_ME), .en(not_1_out), .Q(REG_RS_VAL_WB), .clk(CLOCK), .clr(CLEAR));
  Register #(.width(32)) register_2 (.D(PC_PLUS4_ME), .en(not_1_out), .Q(PC_PLUS4_WB), .clk(CLOCK), .clr(CLEAR));
  Register #(.width(1)) register_3 (.D(PRINT_SC_ME), .en(not_1_out), .Q(PRINT_SC_WB), .clk(CLOCK), .clr(CLEAR));
  Register #(.width(1)) register_4 (.D(HALT_ME), .en(not_1_out), .Q(HALT_WB), .clk(CLOCK), .clr(CLEAR));
  Register #(.width(32)) register_5 (.D(ALURESULT_ME), .en(not_1_out), .Q(ALURESULT_WB), .clk(CLOCK), .clr(CLEAR));
  Register #(.width(1)) register_6 (.D(REGWRITE_ME), .en(not_1_out), .Q(REGWRITE_WB), .clk(CLOCK), .clr(CLEAR));
  Register #(.width(1)) register_7 (.D(JAL_ME), .en(not_1_out), .Q(JAL_WB), .clk(CLOCK), .clr(CLEAR));
  Register #(.width(1)) register_8 (.D(MEM_TO_REG_ME), .en(not_1_out), .Q(MEM_TO_REG_WB), .clk(CLOCK), .clr(CLEAR));
  not not_1 (not_1_out, STALL);
  Register #(.width(32)) register_9 (.D(JUMP_ADDR_ME), .en(not_1_out), .Q(JUMP_ADDR_WB), .clk(CLOCK), .clr(CLEAR));
  Register #(.width(5)) register_10 (
    .D(REG_WRITE_ID_ME), .en(not_1_out), .Q(REG_WRITE_ID_WB), .clk(CLOCK), .clr(CLEAR));
  Register #(.width(1)) register_11 (.D(J_ME), .en(not_1_out), .Q(J_WB), .clk(CLOCK), .clr(CLEAR));
  Register #(.width(1)) register_12 (.D(JR_ME), .en(not_1_out), .Q(JR_WB), .clk(CLOCK), .clr(CLEAR));
  Register #(.width(32)) register_13 (.D(MEM_DATA_ME), .en(not_1_out), .Q(MEM_DATA_WB), .clk(CLOCK), .clr(CLEAR));
endmodule

module Hazard_Unit (
  input  CLOCK,
  input  EX_MEM_REGWRITE,
  input  ID_EX_MEMWRITE,
  input  MEM_WB_REGWRITE,
  input  [4:0] EX_MEM_REGISTER_RD,
  input  [4:0] ID_EX_REGISTER_RS,
  input  [5:0] ID_OPCODE,
  input  [4:0] ID_EX_REGISTER_RT,
  input  [4:0] MEM_WB_REGISTER_RD,
  output [1:0] FORWARD_A,
  output [1:0] FORWARD_B,
  output STALL
);

  Stall_Engine stall_engine_1 (.CLOCK(CLOCK), .ID_OPCODE(ID_OPCODE), .STALL(STALL));
  Forward_Engine forward_engine_1 (
    .EX_MEM_REGWRITE(EX_MEM_REGWRITE), .MEM_WB_REGWRITE(MEM_WB_REGWRITE),
    .EX_MEM_REGISTER_RD(EX_MEM_REGISTER_RD), .ID_EX_REGISTER_RS(ID_EX_REGISTER_RS),
    .ID_EX_REGISTER_RT(ID_EX_REGISTER_RT), .MEM_WB_REGISTER_RD(MEM_WB_REGISTER_RD),
    .ForwardA_1(FORWARD_A[1]), .ForwardA_0(FORWARD_A[0]), .ForwardB_1(FORWARD_B[1]),
    .ForwardB_0(FORWARD_B[0]), .ID_EX_MEMWRITE(ID_EX_MEMWRITE));
endmodule

module Forward_Engine (
  input  ID_EX_MEMWRITE,
  input  EX_MEM_REGWRITE,
  input  MEM_WB_REGWRITE,
  input  [4:0] EX_MEM_REGISTER_RD,
  input  [4:0] ID_EX_REGISTER_RS,
  input  [4:0] ID_EX_REGISTER_RT,
  input  [4:0] MEM_WB_REGISTER_RD,
  output ForwardA_1,
  output ForwardB_1,
  output ForwardA_0,
  output ForwardB_0
);

  wire and_2_out, and_3_out, and_5_out, and_7_out, comparator_1_eq, comparator_2_eq, comparator_3_eq,
       comparator_4_eq, comparator_5_eq, comparator_6_eq, comparator_7_eq, EM_RD__0, MW_RD__0, not_3_out,
       not_4_out, SIG;

  Comparator #(.width(5), .mode("unsigned")) comparator_1 (
    .a(EX_MEM_REGISTER_RD), .b(ID_EX_REGISTER_RS), .eq(comparator_1_eq));  // open: gt, lt
  Comparator #(.width(5), .mode("unsigned")) comparator_2 (
    .a(EX_MEM_REGISTER_RD), .b(ID_EX_REGISTER_RT), .eq(comparator_2_eq));  // open: gt, lt
  // NOT_Gate not_1 is placed but not wired
  // NOT_Gate not_2 is placed but not wired
  Comparator #(.width(5)) comparator_3 (
    .a(MEM_WB_REGISTER_RD), .b(ID_EX_REGISTER_RT), .eq(comparator_3_eq));  // open: gt, lt
  and and_1 (SIG, ID_EX_MEMWRITE, comparator_3_eq, MEM_WB_REGWRITE);
  or or_1 (EM_RD__0, EX_MEM_REGISTER_RD[0], EX_MEM_REGISTER_RD[1], EX_MEM_REGISTER_RD[2], EX_MEM_REGISTER_RD[3], EX_MEM_REGISTER_RD[4]);
  or or_2 (MW_RD__0, MEM_WB_REGISTER_RD[0], MEM_WB_REGISTER_RD[1], MEM_WB_REGISTER_RD[2], MEM_WB_REGISTER_RD[3], MEM_WB_REGISTER_RD[4]);
  and and_2 (and_2_out, EX_MEM_REGWRITE, comparator_1_eq, EM_RD__0);
  and and_3 (and_3_out, EX_MEM_REGWRITE, comparator_2_eq, EM_RD__0);
  not not_3 (not_3_out, and_2_out);
  not not_4 (not_4_out, and_3_out);
  Comparator #(.width(5), .mode("unsigned")) comparator_4 (
    .a(EX_MEM_REGISTER_RD), .b(ID_EX_REGISTER_RS), .eq(comparator_4_eq));  // open: gt, lt
  Comparator #(.width(5), .mode("unsigned")) comparator_5 (
    .a(EX_MEM_REGISTER_RD), .b(ID_EX_REGISTER_RT), .eq(comparator_5_eq));  // open: gt, lt
  Comparator #(.width(5), .mode("unsigned")) comparator_6 (
    .a(MEM_WB_REGISTER_RD), .b(ID_EX_REGISTER_RS), .eq(comparator_6_eq));  // open: gt, lt
  Comparator #(.width(5), .mode("unsigned")) comparator_7 (
    .a(MEM_WB_REGISTER_RD), .b(ID_EX_REGISTER_RT), .eq(comparator_7_eq));  // open: gt, lt
  and and_4 (ForwardA_1, EX_MEM_REGWRITE, comparator_4_eq, EM_RD__0);
  and and_5 (and_5_out, EM_RD__0, comparator_5_eq, EX_MEM_REGWRITE);
  or or_3 (ForwardB_1, and_5_out, SIG);
  and and_6 (ForwardA_0, MEM_WB_REGWRITE, comparator_6_eq, not_3_out, MW_RD__0);
  and and_7 (and_7_out, MW_RD__0, comparator_7_eq, not_4_out, MEM_WB_REGWRITE);
  or or_4 (ForwardB_0, and_7_out, SIG);
endmodule

module Stall_Engine (
  input  CLOCK,
  input  [5:0] ID_OPCODE,
  output STALL
);

  wire and_1_out, and_2_out, and_3_out, and_4_out, and_5_out, d_ff_1_q, n3_cycles_1_out, n4_cycles_1_out,
       n4_cycles_2_out, n4_cycles_3_out, not_1_out, not_2_out, not_3_out, not_4_out, not_5_out, not_6_out,
       not_7_out, not_8_out, not_9_out, not_10_out, not_11_out, not_12_out, not_13_out, not_14_out,
       not_15_out, not_16_out, not_17_out, not_18_out, not_19_out, or_1_out;

  not not_1 (not_1_out, ID_OPCODE[0]);
  not not_2 (not_2_out, ID_OPCODE[2]);
  not not_3 (not_3_out, ID_OPCODE[3]);
  not not_4 (not_4_out, ID_OPCODE[4]);
  not not_5 (not_5_out, ID_OPCODE[5]);
  not not_6 (not_6_out, ID_OPCODE[2]);
  not not_7 (not_7_out, ID_OPCODE[1]);
  not not_8 (not_8_out, ID_OPCODE[2]);
  not not_9 (not_9_out, ID_OPCODE[3]);
  not not_10 (not_10_out, ID_OPCODE[4]);
  not not_11 (not_11_out, ID_OPCODE[5]);
  not not_12 (not_12_out, ID_OPCODE[0]);
  not not_13 (not_13_out, ID_OPCODE[1]);
  not not_14 (not_14_out, ID_OPCODE[3]);
  not not_15 (not_15_out, ID_OPCODE[4]);
  not not_16 (not_16_out, ID_OPCODE[5]);
  not not_17 (not_17_out, ID_OPCODE[2]);
  not not_18 (not_18_out, ID_OPCODE[3]);
  not not_19 (not_19_out, ID_OPCODE[4]);
  and and_1 (and_1_out, not_1_out, ID_OPCODE[1], not_2_out, not_3_out, not_4_out, not_5_out);
  and and_2 (and_2_out, not_5_out, not_4_out, not_3_out, not_6_out, ID_OPCODE[1], ID_OPCODE[0]);
  and and_3 (and_3_out, not_7_out, not_8_out, not_9_out, ID_OPCODE[0], not_10_out, not_11_out);
  and and_4 (and_4_out, not_12_out, not_13_out, ID_OPCODE[2], not_14_out, not_15_out, not_16_out);
  and and_5 (and_5_out, ID_OPCODE[0], ID_OPCODE[1], not_17_out, not_18_out, not_19_out, ID_OPCODE[5]);
  _4_CYCLES u_4_cycles_1 (.VAL(and_1_out), .CLOCK(CLOCK), .OUT(n4_cycles_1_out));
  _4_CYCLES u_4_cycles_2 (.VAL(and_2_out), .CLOCK(CLOCK), .OUT(n4_cycles_2_out));
  _4_CYCLES u_4_cycles_3 (.VAL(and_3_out), .CLOCK(CLOCK), .OUT(n4_cycles_3_out));
  _3_CYCLES u_3_cycles_1 (.VAL(and_4_out), .CLOCK(CLOCK), .OUT(n3_cycles_1_out));
  D_Flip_Flop d_ff_1 (.clk(CLOCK), .D(and_5_out), .Q(d_ff_1_q));  // open: Qn, preset, en, reset
  buf or_1 (or_1_out, and_5_out);  // OR_Gate
  or or_2 (STALL, n4_cycles_1_out, n4_cycles_2_out, n4_cycles_3_out, n3_cycles_1_out, or_1_out);
endmodule

module _4_CYCLES (
  input  VAL,
  input  CLOCK,
  output OUT
);

  wire d_ff_1_q, d_ff_2_q, d_ff_3_q;

  D_Flip_Flop d_ff_1 (.clk(CLOCK), .D(VAL), .Q(d_ff_1_q));  // open: Qn, preset, en, reset
  D_Flip_Flop d_ff_2 (.clk(CLOCK), .D(d_ff_1_q), .Q(d_ff_2_q));  // open: Qn, preset, en, reset
  D_Flip_Flop d_ff_3 (.clk(CLOCK), .D(d_ff_2_q), .Q(d_ff_3_q));  // open: Qn, preset, en, reset
  or or_1 (OUT, VAL, d_ff_1_q, d_ff_2_q, d_ff_3_q);
endmodule

module _3_CYCLES (
  input  VAL,
  input  CLOCK,
  output OUT
);

  wire d_ff_1_q, d_ff_2_q;

  D_Flip_Flop d_ff_1 (.clk(CLOCK), .D(VAL), .Q(d_ff_1_q));  // open: Qn, preset, en, reset
  D_Flip_Flop d_ff_2 (.clk(CLOCK), .D(d_ff_1_q), .Q(d_ff_2_q));  // open: Qn, preset, en, reset
  or or_1 (OUT, VAL, d_ff_2_q, d_ff_1_q);
endmodule

module test (
  input  in_1,
  input  in_2,
  input  in_3,
  input  in_4,
  input  in_5,
  input  in_6,
  input  in_7,
  output out_8,
  output out_9
);

  wire multiplexer_2_out;

  Multiplexer #(.enable("false")) multiplexer_1 (.in0(in_1), .in1(in_2), .out(out_8), .sel(in_6));
  Multiplexer #(.enable("false")) multiplexer_2 (.in0(in_3), .in1(in_4), .out(multiplexer_2_out), .sel(in_6));
  Multiplexer #(.enable("false")) multiplexer_3 (.in0(out_8), .in1(multiplexer_2_out), .out(out_9), .sel(in_7));
  LED led_1 (.in(in_5));
endmodule
